// Logisim project processor.circ as structural Verilog: 10 circuits, main circuit processor
module processor (
  output [15:0] R0,
  output [15:0] R1
);

  wire alu_1_carry, alu_1_zero, clock_1_out, control_1_alustore, control_1_branch, control_1_destdef,
       control_1_immediate, control_1_immstore, control_1_ld, control_1_sourcedef, control_1_st_pc,
       control_1_str, control_1_we;
  wire [3:0] control_1_destreg, control_1_sourcereg, multiplexer_2_out, multiplexer_3_out;
  wire [4:0] control_1_alu_ctrl;
  wire [15:0] alu_1_out, imreg_1_imediate, multiplexer_1_out, multiplexer_4_out, multiplexer_5_out,
       pc_logic_1_act_pc, pc_logic_1_next_seq_pc, ram_1_data, registers_1_dest_2, registers_1_source_2,
       rom_1_data;

  Clock clock_1 (.out(clock_1_out));
  PC_logic pc_logic_1 (
    .ALU_out(alu_1_out), .act_PC(pc_logic_1_act_pc), .next_seq_PC(pc_logic_1_next_seq_pc),
    .Takt(clock_1_out), .rel_jmp(1'b0), .abs_jmp(1'b0));
  ROM #(.addrWidth(16), .dataWidth(16)) rom_1 (.addr(pc_logic_1_act_pc), .data(rom_1_data));  // open: sel
  Multiplexer #(.width(16), .enable("false")) multiplexer_1 (
    .in0(multiplexer_4_out), .in1(pc_logic_1_next_seq_pc), .out(multiplexer_1_out), .sel(control_1_st_pc));
  imReg imreg_1 (.instruction(rom_1_data), .En(control_1_immstore), .Takt(clock_1_out), .imediate(imreg_1_imediate));
  Multiplexer #(.width(4), .enable("false")) multiplexer_2 (
    .in0(rom_1_data[3:0]), .in1(control_1_sourcereg), .out(multiplexer_2_out), .sel(control_1_sourcedef));
  Multiplexer #(.width(4), .enable("false")) multiplexer_3 (
    .in0(rom_1_data[7:4]), .in1(control_1_destreg), .out(multiplexer_3_out), .sel(control_1_destdef));
  control control_1 (
    .Opcode(rom_1_data[15:9]), .WE(control_1_we), .ALUStore(control_1_alustore),
    .immediate(control_1_immediate), .ALU_ctrl(control_1_alu_ctrl), .branch(control_1_branch),
    .str(control_1_str), .ld(control_1_ld), .ST_PC(control_1_st_pc), .SourceDef(control_1_sourcedef),
    .DestDef(control_1_destdef), .SourceReg(control_1_sourcereg), .DestReg(control_1_destreg),
    .ImmStore(control_1_immstore));
  Multiplexer #(.width(16), .enable("false")) multiplexer_4 (
    .in0(ram_1_data), .in1(alu_1_out), .out(multiplexer_4_out), .sel(control_1_alustore));
  registers registers_1 (
    .Write(multiplexer_1_out), .dest_2(registers_1_dest_2), .source_2(registers_1_source_2),
    .WE(control_1_we), .dest(multiplexer_3_out), .Clock(clock_1_out), .R0(R0), .R1(R1),
    .source(multiplexer_2_out));
  Multiplexer #(.width(16), .enable("false")) multiplexer_5 (
    .in0(registers_1_source_2), .in1(imreg_1_imediate), .out(multiplexer_5_out), .sel(control_1_immediate));
  ALU alu_1 (
    .A(registers_1_dest_2), .B(multiplexer_5_out), .Out(alu_1_out), .Zero(alu_1_zero), .Carry(alu_1_carry),
    .Takt(clock_1_out), .SelOp(control_1_alu_ctrl));
  branch branch_1 (.Kind(rom_1_data[3:0]), .C(alu_1_carry), .Z(alu_1_zero), .Enable(control_1_branch));  // open: Jmp
  RAM #(.addrWidth(16), .dataWidth(16), .bus("separate")) ram_1 (
    .addr(alu_1_out), .din(registers_1_source_2), .data(ram_1_data), .str(control_1_str), .clk(clock_1_out),
    .ld(control_1_ld));  // open: sel, clr

  // Notes on the sheet:
  //   Programm
  //   contents of rom_1 (hex, n*v repeats v):
  //   8001 1000 8002 1001 8007 1400 410
  //   RAM
endmodule

module registers (
  input  [15:0] Write,
  input  [3:0] source,
  input  WE,
  input  [3:0] dest,
  input  Clock,
  output [15:0] R0,
  output [15:0] R1,
  output [15:0] dest_2,
  output [15:0] source_2
);

  wire demultiplexer_1_out0, demultiplexer_1_out1, demultiplexer_1_out2, demultiplexer_1_out3,
       demultiplexer_1_out4, demultiplexer_1_out5, demultiplexer_1_out6, demultiplexer_1_out7,
       demultiplexer_1_out8, demultiplexer_1_out9, demultiplexer_1_out10, demultiplexer_1_out11,
       demultiplexer_1_out12, demultiplexer_1_out13, demultiplexer_1_out14, demultiplexer_1_out15;
  wire [15:0] R0_2_q, R1_2_q, R2_2_q, R2_q, R3_2_q, R3_q, R4_2_q, R4_q, R5_2_q, R5_q, R6_2_q, R6_q, R7_2_q,
       R7_q;

  Demultiplexer #(.select(4), .enable("false")) demultiplexer_1 (
    .out0(demultiplexer_1_out0), .out1(demultiplexer_1_out1), .out2(demultiplexer_1_out2),
    .out3(demultiplexer_1_out3), .out4(demultiplexer_1_out4), .out5(demultiplexer_1_out5),
    .out6(demultiplexer_1_out6), .out7(demultiplexer_1_out7), .out8(demultiplexer_1_out8),
    .out9(demultiplexer_1_out9), .out10(demultiplexer_1_out10), .out11(demultiplexer_1_out11),
    .out12(demultiplexer_1_out12), .out13(demultiplexer_1_out13), .out14(demultiplexer_1_out14),
    .out15(demultiplexer_1_out15), .in(WE), .sel(dest));
  Register #(.width(16)) u_R0 (.D(Write), .en(demultiplexer_1_out0), .Q(R0), .clk(Clock));  // open: clr
  Register #(.width(16)) u_R1 (.D(Write), .en(demultiplexer_1_out1), .Q(R1), .clk(Clock));  // open: clr
  Register #(.width(16)) R2 (.D(Write), .en(demultiplexer_1_out2), .Q(R2_q), .clk(Clock));  // open: clr
  Register #(.width(16)) R3 (.D(Write), .en(demultiplexer_1_out3), .Q(R3_q), .clk(Clock));  // open: clr
  Register #(.width(16)) R4 (.D(Write), .en(demultiplexer_1_out4), .Q(R4_q), .clk(Clock));  // open: clr
  Register #(.width(16)) R5 (.D(Write), .en(demultiplexer_1_out5), .Q(R5_q), .clk(Clock));  // open: clr
  Register #(.width(16)) R6 (.D(Write), .en(demultiplexer_1_out6), .Q(R6_q), .clk(Clock));  // open: clr
  Register #(.width(16)) R7 (.D(Write), .en(demultiplexer_1_out7), .Q(R7_q), .clk(Clock));  // open: clr
  Register #(.width(16)) R0_2 (.D(Write), .en(demultiplexer_1_out8), .Q(R0_2_q), .clk(Clock));  // open: clr
  Register #(.width(16)) R1_2 (.D(Write), .en(demultiplexer_1_out9), .Q(R1_2_q), .clk(Clock));  // open: clr
  Register #(.width(16)) R2_2 (.D(Write), .en(demultiplexer_1_out10), .Q(R2_2_q), .clk(Clock));  // open: clr
  Register #(.width(16)) R3_2 (.D(Write), .en(demultiplexer_1_out11), .Q(R3_2_q), .clk(Clock));  // open: clr
  Register #(.width(16)) R4_2 (.D(Write), .en(demultiplexer_1_out12), .Q(R4_2_q), .clk(Clock));  // open: clr
  Register #(.width(16)) R5_2 (.D(Write), .en(demultiplexer_1_out13), .Q(R5_2_q), .clk(Clock));  // open: clr
  Register #(.width(16)) R6_2 (.D(Write), .en(demultiplexer_1_out14), .Q(R6_2_q), .clk(Clock));  // open: clr
  Register #(.width(16)) R7_2 (.D(Write), .en(demultiplexer_1_out15), .Q(R7_2_q), .clk(Clock));  // open: clr
  Multiplexer #(.select(4), .width(16), .enable("false")) multiplexer_1 (
    .in0(R0), .in1(R1), .in2(R2_q), .in3(R3_q), .in4(R4_q), .in5(R5_q), .in6(R6_q), .in7(R7_q), .in8(R0_2_q),
    .in9(R1_2_q), .in10(R2_2_q), .in11(R3_2_q), .in12(R4_2_q), .in13(R5_2_q), .in14(R6_2_q), .in15(R7_2_q),
    .out(dest_2), .sel(dest));
  Multiplexer #(.select(4), .width(16), .enable("false")) multiplexer_2 (
    .in0(R0), .in1(R1), .in2(R2_q), .in3(R3_q), .in4(R4_q), .in5(R5_q), .in6(R6_q), .in7(R7_q), .in8(R0_2_q),
    .in9(R1_2_q), .in10(R2_2_q), .in11(R3_2_q), .in12(R4_2_q), .in13(R5_2_q), .in14(R6_2_q), .in15(R7_2_q),
    .out(source_2), .sel(source));
endmodule

module ALU (
  input  [15:0] A,
  input  [15:0] B,
  input  Takt,
  input  [4:0] SelOp,
  output [15:0] Out,
  output Zero,
  output Carry
);

  wire adder_1_cout, and_2_out, lsl_1_msb_out, lsr_1_lsb_out, multiplexer_1_out, multiplexer_2_out, or_2_out,
       subtractor_1_bout;
  wire [15:0] adder_1_out, and_1_out, lsl_1_out, lsr_1_out, or_1_out, subtractor_1_out, xor_1_out;

  Adder #(.width(16)) adder_1 (.a(A), .b(B), .out(adder_1_out), .cin(and_2_out), .cout(adder_1_cout));
  Subtractor #(.width(16)) subtractor_1 (
    .a(A), .b(B), .out(subtractor_1_out), .bin(and_2_out), .bout(subtractor_1_bout));
  assign and_1_out = A & B;  // AND_Gate and_1, 16 bits wide
  assign or_1_out = A | B;  // OR_Gate or_1, 16 bits wide
  assign xor_1_out = A ^ B;  // XOR_Gate xor_1, 16 bits wide
  LSL lsl_1 (.LSB_In(and_2_out), .Data(A), .Out(lsl_1_out), .MSB_Out(lsl_1_msb_out));
  LSR lsr_1 (.Data(A), .MSB_In(and_2_out), .LSB_Out(lsr_1_lsb_out), .Out(lsr_1_out));
  Multiplexer #(.select(3), .enable("false")) multiplexer_1 (
    .in0(1'b0), .in1(adder_1_cout), .in2(subtractor_1_bout), .in3(1'b0), .in4(1'b0), .in5(1'b0),
    .in6(lsl_1_msb_out), .in7(lsr_1_lsb_out), .out(multiplexer_1_out), .sel(SelOp[2:0]));
  Multiplexer #(.select(3), .enable("false")) multiplexer_2 (
    .in0(1'b0), .in1(1'b1), .in2(1'b1), .in3(1'b0), .in4(1'b0), .in5(1'b0), .in6(1'b1), .in7(1'b1),
    .out(multiplexer_2_out), .sel(SelOp[2:0]));
  and and_2 (and_2_out, SelOp[4], Carry);
  D_Flip_Flop u_Carry (
    .clk(Takt), .D(multiplexer_1_out), .Q(Carry), .en(multiplexer_2_out));  // open: Qn, preset, reset
  Multiplexer #(.select(3), .width(16), .enable("false")) multiplexer_3 (
    .in0(B), .in1(adder_1_out), .in2(subtractor_1_out), .in3(and_1_out), .in4(or_1_out), .in5(xor_1_out),
    .in6(lsl_1_out), .in7(lsr_1_out), .out(Out), .sel(SelOp[2:0]));
  or or_2 (or_2_out, Out[0], Out[1], Out[2], Out[3], Out[4], Out[5], Out[6], Out[7], Out[9], Out[10], Out[11], Out[12], Out[13], Out[14], Out[15], Out[8]);
  D_Flip_Flop u_Zero (.clk(Takt), .D(or_2_out), .Qn(Zero));  // open: Q, preset, en, reset
endmodule

module LSL (
  input  LSB_In,
  input  [15:0] Data,
  output [15:0] Out,
  output MSB_Out
);


  assign MSB_Out = Data[15];
  assign Out = {Data[14:0], LSB_In};
endmodule

module LSR (
  input  [15:0] Data,
  input  MSB_In,
  output LSB_Out,
  output [15:0] Out
);


  assign LSB_Out = Data[0];
  assign Out = {MSB_In, Data[15:1]};
endmodule

module branch (
  input  C,
  input  Z,
  input  [3:0] Kind,
  input  Enable,
  output Jmp
);

  wire multiplexer_1_out, xor_1_out;

  and and_1 (Jmp, xor_1_out, Enable);
  xor xor_1 (xor_1_out, Kind[2], multiplexer_1_out);
  Multiplexer #(.select(2), .enable("false")) multiplexer_1 (
    .in0(1'b1), .in1(C), .in2(Z), .in3(1'b1), .out(multiplexer_1_out), .sel(Kind[1:0]));
endmodule

module control (
  input  [6:0] Opcode,
  output ImmStore,
  output DestDef,
  output [3:0] DestReg,
  output SourceDef,
  output [3:0] SourceReg,
  output ALUStore,
  output immediate,
  output [4:0] ALU_ctrl,
  output WE,
  output branch,
  output ST_PC,
  output str,
  output ld
);

  wire [5:0] multiplexer_1_out;
  wire [23:22] rom_1_data;

  Multiplexer #(.width(6), .enable("false")) multiplexer_1 (
    .in0(Opcode[5:0]), .in1({6{1'b0}}), .out(multiplexer_1_out), .sel(Opcode[6]));
  ROM #(.addrWidth(6), .dataWidth(24)) rom_1 (
    .addr(multiplexer_1_out),
    .data({rom_1_data, DestReg, SourceReg, ALU_ctrl, DestDef, SourceDef, ST_PC, WE, ALUStore, immediate, branch, str, ld}));  // open: sel

  assign ImmStore = Opcode[6];

  // Notes on the sheet:
  //   contents of rom_1 (hex, n*v repeats v):
  //   0 20 220 1220 420 1420 620 820 28 a20 228 1228 428 1428 628 828 a28
endmodule

module graphic (
  input  [7:0] Data,
  input  Takt,
  input  Enable,
  input  [7:0] Addr,
  output [7:0] out_5,
  output [7:0] out_6,
  output [7:0] out_7,
  output [7:0] out_8,
  output [7:0] out_9,
  output [7:0] out_10,
  output [7:0] out_11,
  output [7:0] out_12,
  output [7:0] out_13,
  output [7:0] out_14,
  output [7:0] out_15,
  output [7:0] out_16,
  output [7:0] out_17,
  output [7:0] out_18,
  output [7:0] out_19,
  output [7:0] out_20
);

  wire demultiplexer_1_out0, demultiplexer_1_out1, demultiplexer_1_out2, demultiplexer_1_out3,
       demultiplexer_1_out4, demultiplexer_1_out5, demultiplexer_1_out6, demultiplexer_1_out7,
       demultiplexer_1_out8, demultiplexer_1_out9, demultiplexer_1_out10, demultiplexer_1_out11,
       demultiplexer_1_out12, demultiplexer_1_out13, demultiplexer_1_out14, demultiplexer_1_out15,
       demultiplexer_1_out16;
  wire [7:0] register_1_q, register_2_q, register_3_q, register_4_q, register_5_q, register_6_q,
       register_7_q, register_8_q, register_9_q, register_10_q, register_11_q, register_12_q, register_13_q,
       register_14_q, register_15_q, register_16_q;

  Demultiplexer #(.select(5), .enable("false")) demultiplexer_1 (
    .out0(demultiplexer_1_out0), .out1(demultiplexer_1_out1), .out2(demultiplexer_1_out2),
    .out3(demultiplexer_1_out3), .out4(demultiplexer_1_out4), .out5(demultiplexer_1_out5),
    .out6(demultiplexer_1_out6), .out7(demultiplexer_1_out7), .out8(demultiplexer_1_out8),
    .out9(demultiplexer_1_out9), .out10(demultiplexer_1_out10), .out11(demultiplexer_1_out11),
    .out12(demultiplexer_1_out12), .out13(demultiplexer_1_out13), .out14(demultiplexer_1_out14),
    .out15(demultiplexer_1_out15), .out16(demultiplexer_1_out16), .in(Enable), .sel(Addr[4:0]));  // open: out17, out18, out19, out20, out21, out22, out23, out24, out25, out26, out27, out28, out29, out30, out31
  Register register_1 (.D(Data), .en(demultiplexer_1_out0), .Q(register_1_q), .clk(Takt));  // open: clr
  Register register_2 (.D(Data), .en(demultiplexer_1_out1), .Q(register_2_q), .clk(Takt));  // open: clr
  Register register_3 (.D(Data), .en(demultiplexer_1_out2), .Q(register_3_q), .clk(Takt));  // open: clr
  Register register_4 (.D(Data), .en(demultiplexer_1_out3), .Q(register_4_q), .clk(Takt));  // open: clr
  Register register_5 (.D(Data), .en(demultiplexer_1_out4), .Q(register_5_q), .clk(Takt));  // open: clr
  Register register_6 (.D(Data), .en(demultiplexer_1_out5), .Q(register_6_q), .clk(Takt));  // open: clr
  Register register_7 (.D(Data), .en(demultiplexer_1_out6), .Q(register_7_q), .clk(Takt));  // open: clr
  Register register_8 (.D(Data), .en(demultiplexer_1_out7), .Q(register_8_q), .clk(Takt));  // open: clr
  Register register_9 (.D(Data), .en(demultiplexer_1_out8), .Q(register_9_q), .clk(Takt));  // open: clr
  Register register_10 (.D(Data), .en(demultiplexer_1_out9), .Q(register_10_q), .clk(Takt));  // open: clr
  Register register_11 (.D(Data), .en(demultiplexer_1_out10), .Q(register_11_q), .clk(Takt));  // open: clr
  Register register_12 (.D(Data), .en(demultiplexer_1_out11), .Q(register_12_q), .clk(Takt));  // open: clr
  Register register_13 (.D(Data), .en(demultiplexer_1_out12), .Q(register_13_q), .clk(Takt));  // open: clr
  Register register_14 (.D(Data), .en(demultiplexer_1_out13), .Q(register_14_q), .clk(Takt));  // open: clr
  Register register_15 (.D(Data), .en(demultiplexer_1_out14), .Q(register_15_q), .clk(Takt));  // open: clr
  Register register_16 (.D(Data), .en(demultiplexer_1_out15), .Q(register_16_q), .clk(Takt));  // open: clr
  Register register_17 (.D(register_1_q), .en(demultiplexer_1_out16), .Q(out_5), .clk(Takt));  // open: clr
  Register register_18 (.D(register_2_q), .en(demultiplexer_1_out16), .Q(out_6), .clk(Takt));  // open: clr
  Register register_19 (.D(register_3_q), .en(demultiplexer_1_out16), .Q(out_7), .clk(Takt));  // open: clr
  Register register_20 (.D(register_4_q), .en(demultiplexer_1_out16), .Q(out_8), .clk(Takt));  // open: clr
  Register register_21 (.D(register_5_q), .en(demultiplexer_1_out16), .Q(out_9), .clk(Takt));  // open: clr
  Register register_22 (.D(register_6_q), .en(demultiplexer_1_out16), .Q(out_10), .clk(Takt));  // open: clr
  Register register_23 (.D(register_7_q), .en(demultiplexer_1_out16), .Q(out_11), .clk(Takt));  // open: clr
  Register register_24 (.D(register_8_q), .en(demultiplexer_1_out16), .Q(out_12), .clk(Takt));  // open: clr
  Register register_25 (.D(register_9_q), .en(demultiplexer_1_out16), .Q(out_13), .clk(Takt));  // open: clr
  Register register_26 (.D(register_10_q), .en(demultiplexer_1_out16), .Q(out_14), .clk(Takt));  // open: clr
  Register register_27 (.D(register_11_q), .en(demultiplexer_1_out16), .Q(out_15), .clk(Takt));  // open: clr
  Register register_28 (.D(register_12_q), .en(demultiplexer_1_out16), .Q(out_16), .clk(Takt));  // open: clr
  Register register_29 (.D(register_13_q), .en(demultiplexer_1_out16), .Q(out_17), .clk(Takt));  // open: clr
  Register register_30 (.D(register_14_q), .en(demultiplexer_1_out16), .Q(out_18), .clk(Takt));  // open: clr
  Register register_31 (.D(register_15_q), .en(demultiplexer_1_out16), .Q(out_19), .clk(Takt));  // open: clr
  Register register_32 (.D(register_16_q), .en(demultiplexer_1_out16), .Q(out_20), .clk(Takt));  // open: clr
endmodule

module PC_logic (
  input  [15:0] ALU_out,
  input  Takt,
  input  rel_jmp,
  input  abs_jmp,
  output [15:0] next_seq_PC,
  output [15:0] act_PC
);

  wire [15:0] adder_2_out, multiplexer_1_out, multiplexer_2_out;

  Register #(.width(16)) PC (.D(multiplexer_2_out), .Q(act_PC), .clk(Takt));  // open: en, clr
  Adder #(.width(16)) adder_1 (.a(act_PC), .b(16'h1), .out(next_seq_PC));  // open: cin, cout
  Adder #(.width(16)) adder_2 (.a(next_seq_PC), .b(ALU_out), .out(adder_2_out));  // open: cin, cout
  Multiplexer #(.width(16), .enable("false")) multiplexer_1 (
    .in0(next_seq_PC), .in1(adder_2_out), .out(multiplexer_1_out), .sel(rel_jmp));
  Multiplexer #(.width(16), .enable("false")) multiplexer_2 (
    .in0(multiplexer_1_out), .in1(ALU_out), .out(multiplexer_2_out), .sel(abs_jmp));

  // Notes on the sheet:
  //   rel_jmp: pull=down
  //   abs_jmp: pull=down
endmodule

module imReg (
  input  [15:0] instruction,
  input  En,
  input  Takt,
  output [15:0] imediate
);

  wire [15:15] register_1_q;

  Register #(.width(16)) register_1 (
    .D(instruction), .en(En), .Q({register_1_q[15], imediate[14:0]}), .clk(Takt));  // open: clr

  assign imediate[15] = instruction[8];
endmodule
